# Fritzing sketch motor (saved by Fritzing 0.9.3b)
breadboards: 1

parts:
  IC1 = L293D [package=THT]
  M1 = DC Motor
  VCC1 = Battery
  Raspberry_Pi_Zero2 = Raspberry Pi Zero
  M2 = DC Motor

nets:
  N1: IC1.Enable_1, IC1.Enable_2, Raspberry_Pi_Zero2.GPIO3
  N2: IC1.In_1, Raspberry_Pi_Zero2.GPIO23
  N3: IC1.Out_1_(_Controlled_by_Enable_1_), M2.pin_2
  N4: IC1.0V, VCC1.-, Raspberry_Pi_Zero2.GND
  N5: IC1.Out_2_(_Controlled_by_Enable_1_), M2.pin_1
  N6: IC1.In_2, Raspberry_Pi_Zero2.GPIO24
  N7: IC1.+Vmotor, VCC1.+
  N8: IC1.In_3, Raspberry_Pi_Zero2.GPIO15
  N9: IC1.Out_3_(_Controlled_by_Enable_2_), M1.pin_2
  N10: IC1.Out_4_(_Controlled_by_Enable_2_), M1.pin_1
  N11: IC1.In_4, Raspberry_Pi_Zero2.GPIO14
  N12: IC1.+V, Raspberry_Pi_Zero2.5V
